# Fritzing sketch Hydra (saved by Fritzing 0.9.3b)
circuit board: 10cm x 10cm
breadboards: 1

parts:
  J4 = female pin header, 10 pins [form="♀ (female)"]
  J3 = female pin header, 2 pins [form="♀ (female)"]  # not connected
  J5 = female pin header, 2 pins [form="♀ (female)"]  # not connected
  J8 = female pin header, 3 pins [form="♀ (female)"]
  J10 = female pin header, 3 pins [form="♀ (female)"]
  J12 = female pin header, 3 pins [form="♀ (female)"]
  J14 = female pin header, 3 pins [form="♀ (female)"]
  J16 = female pin header, 3 pins [form="♀ (female)"]
  VCC = Generic female header - 10 pins [form="♀ (female)" package=THT]
  Ph = female pin header, 3 pins [form="♀ (female)"]
  ORP = female pin header, 3 pins [form="♀ (female)"]
  DO = female pin header, 3 pins [form="♀ (female)"]
  RTD = female pin header, 3 pins [form="♀ (female)"]
  EC = female pin header, 3 pins [form="♀ (female)"]
  J17 = female pin header, 3 pins [form="♀ (female)"]
  J18 = female pin header, 3 pins [form="♀ (female)"]
  J19 = female pin header, 3 pins [form="♀ (female)"]
  J20 = female pin header, 3 pins [form="♀ (female)"]
  J21 = female pin header, 3 pins [form="♀ (female)"]
  VCC_2 = female pin header, 5 pins [form="♀ (female)"]
  J28 = female pin header, 5 pins [form="♀ (female)"]
  J24 = female pin header, 5 pins [form="♀ (female)"]
  J23 = female pin header, 5 pins [form="♀ (female)"]
  J26 = female pin header, 5 pins [form="♀ (female)"]
  VCC_3 = female pin header, 5 pins [form="♀ (female)"]
  VCC_4 = female pin header, 5 pins [form="♀ (female)"]
  VCC_5 = female pin header, 5 pins [form="♀ (female)"]
  NodeMCU = Generic female header - 10 pins [form="♀ (female)" package=THT]
  VCC2 = Generic female header - 10 pins [form="♀ (female)" package=THT]  # not connected
  VCC3 = female pin header, 5 pins [form="♀ (female)"]
  VCC4 = female pin header, 5 pins [form="♀ (female)"]
  5V+ = Screw terminal - 2 pins [package=THT]

nets:
  N1: J4.pin1, J24.pin1
  N2: J4.pin2, J24.pin2
  N3: J4.pin3, J23.pin1
  N4: J4.pin4, J23.pin2
  N5: J4.pin5, J26.pin1
  N6: J4.pin6, J26.pin2
  N7: J4.pin7, J28.pin1
  N8: J4.pin8, J28.pin2
  N9: J4.pin9, J8.pin1
  N10: J4.pin10, J8.pin2
  N11: J10.pin1, VCC_2.pin1
  N12: J10.pin2, VCC_2.pin2
  N13: J10.pin3, VCC_2.pin3
  N14: J12.pin1, VCC_3.pin1
  N15: J12.pin2, VCC_3.pin2
  N16: J12.pin3, VCC_3.pin3
  N17: J14.pin1, VCC_4.pin1
  N18: J14.pin2, VCC_4.pin2
  N19: J14.pin3, VCC_4.pin3
  N20: J16.pin1, VCC_5.pin1
  N21: J16.pin2, VCC_5.pin2
  N22: J16.pin3, VCC_5.pin3
  N23: VCC.VCC, VCC4.pin5
  N24: VCC.RX_in, NodeMCU.RX_8
  N25: VCC.TX_in, NodeMCU.GND
  N26: VCC.S1, NodeMCU.S1
  N27: VCC.S2, NodeMCU.TX_in
  N28: VCC.S3, NodeMCU.RX_in
  N29: Ph.pin1, J21.pin1
  N30: Ph.pin2, J21.pin2
  N31: Ph.pin3, VCC_4.pin5
  N32: ORP.pin1, J17.pin1
  N33: ORP.pin2, J17.pin2
  N34: ORP.pin3, VCC_5.pin5
  N35: DO.pin1, J19.pin1
  N36: DO.pin2, J19.pin2
  N37: DO.pin3, VCC_3.pin5
  N38: RTD.pin1, J20.pin1
  N39: RTD.pin2, J20.pin2
  N40: RTD.pin3, J28.pin5, J24.pin5, J23.pin5, J26.pin5, VCC3.pin1
  N41: EC.pin1, J18.pin1
  N42: EC.pin2, J18.pin2
  N43: EC.pin3, VCC_2.pin5
  N44: VCC3.pin5, 5V+.pin1

custom parts:
  Generic female header - 10 pins: Generic female header
